# Fritzing sketch PushButton (saved by Fritzing 0.9.3b)

parts:
  Part1 = Arduino Uno (Rev3) - ICSP
  S1 = Square Pushbutton
  R1 = Resistor [tolerance=±5% resistance=220 package="0603 [SMD]"]

nets:
  N1: Part1.D4, S1.leg1
  N2: Part1.3V3, R1.Pin_0
  N3: S1.leg0, R1.Pin_1
