# Fritzing sketch Tilt (saved by Fritzing 0.9.3b)

parts:
  Part1 = Arduino Uno (Rev3) - ICSP
  S1 = Tilt Switch [package=THT]
  LED1 = LED - 5mm [color="Red (633nm)" package="5 mm [THT]"]

nets:
  N1: Part1.D10_PWM/SS, LED1.anode
  N2: Part1.GND, LED1.cathode
  N3: Part1.D2, S1.Pin_1
  N4: Part1.3V3, S1.Pin_2
