# Fritzing sketch ultrasonic (saved by Fritzing 0.9.3b)

parts:
  Part1 = Arduino Uno (Rev3)
  hc-sr1 = hc-sr04

nets:
  GND: Part1.GND, hc-sr1.GND
  N1: Part1.D3_PWM, hc-sr1.Trig
  N2: Part1.D4, hc-sr1.Echo
  5V: Part1.5V, hc-sr1.VCC
